# Fritzing sketch fan-controller-circuit (saved by Fritzing 0.9.3b)
breadboards: 1

parts:
  WeMos_D1_Mini1 = WeMos D1 Mini  # not connected
  U1 = TLP621 [package=THT]
  U2 = TLP621 [package=THT]
  U3 = TLP621 [package=THT]  # not connected
  U4 = TLP621 [package=THT]
  U5 = TLP621 [package=THT]
  U6 = TLP621 [package=THT]  # not connected
  U7 = TLP621 [package=THT]  # not connected
  U8 = TLP621 [package=THT]  # not connected
  U9 = TLP621 [package=THT]  # not connected
  R1 = 1k Ω Resistor [package=THT]

nets:
  N1: U1.Pin_1, R1.Pin_0
  N2: U1.Pin_2, U2.Pin_1, U4.Pin_2, U5.Pin_1

custom parts:
  1k Ω Resistor: A generic resistor (0.25W)
